// Logisim project CPU-5.circ as structural Verilog: 12 circuits, main circuit main
module main (
  input  [31:0] in_1,
  output out_2,
  output [1:0] out_3,
  output out_4,
  output [3:0] out_5,
  output out_6,
  output [4:0] out_7,
  output out_8,
  output [4:0] out_9,
  output [1:0] out_10,
  output out_11,
  output out_12,
  output [4:0] out_13
);

  Instruction_Decoder instruction_decoder_1 (
    .BS(out_10), .FS(out_5), .MD(out_3), .PS(out_4), .MW(out_11), .MA(out_6), .DA(out_9), .BA(out_13),
    .AA(out_7), .Instruction_Code(in_1), .CS(out_8), .RW(out_2), .MB(out_12));
endmodule

module Register_File (
  input  [31:0] D_Data,
  input  [4:0] A_Address,
  input  [4:0] B_Address,
  input  Write,
  input  [4:0] D_Address,
  input  CLK,
  output [31:0] A_Data,
  output [31:0] B_Data
);

  wire and_1_out, and_2_out, and_3_out, and_4_out, and_5_out, and_6_out, and_7_out, and_8_out, and_9_out,
       and_10_out, and_11_out, and_12_out, and_13_out, and_14_out, and_15_out, and_16_out, and_17_out,
       and_18_out, and_19_out, and_20_out, and_21_out, and_22_out, and_23_out, and_24_out, and_25_out,
       and_26_out, and_27_out, and_28_out, and_29_out, and_30_out, and_31_out, and_32_out, decoder_1_out0,
       decoder_1_out1, decoder_1_out2, decoder_1_out3, decoder_1_out4, decoder_1_out5, decoder_1_out6,
       decoder_1_out7, decoder_1_out8, decoder_1_out9, decoder_1_out10, decoder_1_out11, decoder_1_out12,
       decoder_1_out13, decoder_1_out14, decoder_1_out15, decoder_1_out16, decoder_1_out17, decoder_1_out18,
       decoder_1_out19, decoder_1_out20, decoder_1_out21, decoder_1_out22, decoder_1_out23, decoder_1_out24,
       decoder_1_out25, decoder_1_out26, decoder_1_out27, decoder_1_out28, decoder_1_out29, decoder_1_out30,
       decoder_1_out31;
  wire [31:0] register_1_q, register_2_q, register_3_q, register_4_q, register_5_q, register_6_q,
       register_7_q, register_8_q, register_9_q, register_10_q, register_11_q, register_12_q, register_13_q,
       register_14_q, register_15_q, register_16_q, register_17_q, register_18_q, register_19_q,
       register_20_q, register_21_q, register_22_q, register_23_q, register_24_q, register_25_q,
       register_26_q, register_27_q, register_28_q, register_29_q, register_30_q, register_31_q,
       register_32_q;

  Decoder #(.select(5)) decoder_1 (
    .out0(decoder_1_out0), .out1(decoder_1_out1), .out2(decoder_1_out2), .out3(decoder_1_out3),
    .out4(decoder_1_out4), .out5(decoder_1_out5), .out6(decoder_1_out6), .out7(decoder_1_out7),
    .out8(decoder_1_out8), .out9(decoder_1_out9), .out10(decoder_1_out10), .out11(decoder_1_out11),
    .out12(decoder_1_out12), .out13(decoder_1_out13), .out14(decoder_1_out14), .out15(decoder_1_out15),
    .out16(decoder_1_out16), .out17(decoder_1_out17), .out18(decoder_1_out18), .out19(decoder_1_out19),
    .out20(decoder_1_out20), .out21(decoder_1_out21), .out22(decoder_1_out22), .out23(decoder_1_out23),
    .out24(decoder_1_out24), .out25(decoder_1_out25), .out26(decoder_1_out26), .out27(decoder_1_out27),
    .out28(decoder_1_out28), .out29(decoder_1_out29), .out30(decoder_1_out30), .out31(decoder_1_out31),
    .sel(D_Address));  // open: en
  and and_1 (and_1_out, decoder_1_out0, Write);
  and and_2 (and_2_out, decoder_1_out1, Write);
  and and_3 (and_3_out, decoder_1_out2, Write);
  and and_4 (and_4_out, decoder_1_out3, Write);
  and and_5 (and_5_out, decoder_1_out4, Write);
  and and_6 (and_6_out, decoder_1_out5, Write);
  and and_7 (and_7_out, decoder_1_out6, Write);
  and and_8 (and_8_out, decoder_1_out7, Write);
  and and_9 (and_9_out, decoder_1_out8, Write);
  and and_10 (and_10_out, decoder_1_out9, Write);
  and and_11 (and_11_out, decoder_1_out10, Write);
  and and_12 (and_12_out, decoder_1_out11, Write);
  and and_13 (and_13_out, decoder_1_out12, Write);
  and and_14 (and_14_out, decoder_1_out13, Write);
  and and_15 (and_15_out, decoder_1_out14, Write);
  and and_16 (and_16_out, decoder_1_out15, Write);
  and and_17 (and_17_out, decoder_1_out16, Write);
  and and_18 (and_18_out, decoder_1_out17, Write);
  and and_19 (and_19_out, decoder_1_out18, Write);
  and and_20 (and_20_out, decoder_1_out19, Write);
  and and_21 (and_21_out, decoder_1_out20, Write);
  and and_22 (and_22_out, decoder_1_out21, Write);
  and and_23 (and_23_out, decoder_1_out22, Write);
  and and_24 (and_24_out, decoder_1_out23, Write);
  and and_25 (and_25_out, decoder_1_out24, Write);
  and and_26 (and_26_out, decoder_1_out25, Write);
  and and_27 (and_27_out, decoder_1_out26, Write);
  and and_28 (and_28_out, decoder_1_out27, Write);
  and and_29 (and_29_out, decoder_1_out28, Write);
  and and_30 (and_30_out, decoder_1_out29, Write);
  and and_31 (and_31_out, decoder_1_out30, Write);
  and and_32 (and_32_out, decoder_1_out31, Write);
  Register #(.width(32)) register_1 (.en(and_1_out), .Q(register_1_q), .clk(CLK));  // open: D, clr
  Register #(.width(32)) register_2 (.D(D_Data), .en(and_2_out), .Q(register_2_q), .clk(CLK));  // open: clr
  Register #(.width(32)) register_3 (.D(D_Data), .en(and_3_out), .Q(register_3_q), .clk(CLK));  // open: clr
  Register #(.width(32)) register_4 (.D(D_Data), .en(and_4_out), .Q(register_4_q), .clk(CLK));  // open: clr
  Register #(.width(32)) register_5 (.D(D_Data), .en(and_5_out), .Q(register_5_q), .clk(CLK));  // open: clr
  Register #(.width(32)) register_6 (.D(D_Data), .en(and_6_out), .Q(register_6_q), .clk(CLK));  // open: clr
  Register #(.width(32)) register_7 (.D(D_Data), .en(and_7_out), .Q(register_7_q), .clk(CLK));  // open: clr
  Register #(.width(32)) register_8 (.D(D_Data), .en(and_8_out), .Q(register_8_q), .clk(CLK));  // open: clr
  Register #(.width(32)) register_9 (.D(D_Data), .en(and_9_out), .Q(register_9_q), .clk(CLK));  // open: clr
  Register #(.width(32)) register_10 (.D(D_Data), .en(and_10_out), .Q(register_10_q), .clk(CLK));  // open: clr
  Register #(.width(32)) register_11 (.D(D_Data), .en(and_11_out), .Q(register_11_q), .clk(CLK));  // open: clr
  Register #(.width(32)) register_12 (.D(D_Data), .en(and_12_out), .Q(register_12_q), .clk(CLK));  // open: clr
  Register #(.width(32)) register_13 (.D(D_Data), .en(and_13_out), .Q(register_13_q), .clk(CLK));  // open: clr
  Register #(.width(32)) register_14 (.D(D_Data), .en(and_14_out), .Q(register_14_q), .clk(CLK));  // open: clr
  Register #(.width(32)) register_15 (.D(D_Data), .en(and_15_out), .Q(register_15_q), .clk(CLK));  // open: clr
  Register #(.width(32)) register_16 (.D(D_Data), .en(and_16_out), .Q(register_16_q), .clk(CLK));  // open: clr
  Register #(.width(32)) register_17 (.D(D_Data), .en(and_17_out), .Q(register_17_q), .clk(CLK));  // open: clr
  Register #(.width(32)) register_18 (.D(D_Data), .en(and_18_out), .Q(register_18_q), .clk(CLK));  // open: clr
  Register #(.width(32)) register_19 (.D(D_Data), .en(and_19_out), .Q(register_19_q), .clk(CLK));  // open: clr
  Register #(.width(32)) register_20 (.D(D_Data), .en(and_20_out), .Q(register_20_q), .clk(CLK));  // open: clr
  Register #(.width(32)) register_21 (.D(D_Data), .en(and_21_out), .Q(register_21_q), .clk(CLK));  // open: clr
  Register #(.width(32)) register_22 (.D(D_Data), .en(and_22_out), .Q(register_22_q), .clk(CLK));  // open: clr
  Register #(.width(32)) register_23 (.D(D_Data), .en(and_23_out), .Q(register_23_q), .clk(CLK));  // open: clr
  Register #(.width(32)) register_24 (.D(D_Data), .en(and_24_out), .Q(register_24_q), .clk(CLK));  // open: clr
  Register #(.width(32)) register_25 (.D(D_Data), .en(and_25_out), .Q(register_25_q), .clk(CLK));  // open: clr
  Register #(.width(32)) register_26 (.D(D_Data), .en(and_26_out), .Q(register_26_q), .clk(CLK));  // open: clr
  Register #(.width(32)) register_27 (.D(D_Data), .en(and_27_out), .Q(register_27_q), .clk(CLK));  // open: clr
  Register #(.width(32)) register_28 (.D(D_Data), .en(and_28_out), .Q(register_28_q), .clk(CLK));  // open: clr
  Register #(.width(32)) register_29 (.D(D_Data), .en(and_29_out), .Q(register_29_q), .clk(CLK));  // open: clr
  Register #(.width(32)) register_30 (.D(D_Data), .en(and_30_out), .Q(register_30_q), .clk(CLK));  // open: clr
  Register #(.width(32)) register_31 (.D(D_Data), .en(and_31_out), .Q(register_31_q), .clk(CLK));  // open: clr
  Register #(.width(32)) register_32 (.D(D_Data), .en(and_32_out), .Q(register_32_q), .clk(CLK));  // open: clr
  Multiplexer #(.select(5), .width(32)) multiplexer_1 (
    .in0(register_1_q), .in1(register_2_q), .in2(register_3_q), .in3(register_4_q), .in4(register_5_q),
    .in5(register_6_q), .in6(register_7_q), .in7(register_8_q), .in8(register_9_q), .in9(register_10_q),
    .in10(register_11_q), .in11(register_12_q), .in12(register_13_q), .in13(register_14_q),
    .in14(register_15_q), .in15(register_16_q), .in16(register_17_q), .in17(register_18_q),
    .in18(register_19_q), .in19(register_20_q), .in20(register_21_q), .in21(register_22_q),
    .in22(register_23_q), .in23(register_24_q), .in24(register_25_q), .in25(register_26_q),
    .in26(register_27_q), .in27(register_28_q), .in28(register_29_q), .in29(register_30_q),
    .in30(register_31_q), .in31(register_32_q), .out(A_Data), .sel(A_Address));  // open: en
  Multiplexer #(.select(5), .width(32)) multiplexer_2 (
    .in0(register_1_q), .in1(register_2_q), .in2(register_3_q), .in3(register_4_q), .in4(register_5_q),
    .in5(register_6_q), .in6(register_7_q), .in7(register_8_q), .in8(register_9_q), .in9(register_10_q),
    .in10(register_11_q), .in11(register_12_q), .in12(register_13_q), .in13(register_14_q),
    .in14(register_15_q), .in15(register_16_q), .in16(register_17_q), .in17(register_18_q),
    .in18(register_19_q), .in19(register_20_q), .in20(register_21_q), .in21(register_22_q),
    .in22(register_23_q), .in23(register_24_q), .in24(register_25_q), .in25(register_26_q),
    .in26(register_27_q), .in27(register_28_q), .in28(register_29_q), .in29(register_30_q),
    .in30(register_31_q), .in31(register_32_q), .out(B_Data), .sel(B_Address));  // open: en
endmodule

module Arithmetic_Circuit (
  input  [31:0] A,
  input  Cin,
  input  [31:0] B,
  input  [1:0] S,
  output [31:0] X,
  output Cout
);

  wire [31:0] multiplexer_1_out, not_1_out;

  assign not_1_out = ~B;  // NOT_Gate not_1, 32 bits wide
  Multiplexer #(.select(2), .width(32)) multiplexer_1 (
    .in0({32{1'b0}}), .in1(B), .in2(not_1_out), .in3({32{1'b1}}), .out(multiplexer_1_out), .sel(S));  // open: en
  Adder #(.width(32)) adder_1 (.a(A), .b(multiplexer_1_out), .out(X), .cin(Cin), .cout(Cout));
endmodule

module Bit_Shifter (
  input  [31:0] B,
  input  [1:0] S,
  output [31:0] H
);

  wire [31:0] shifter_1_out, shifter_2_out;

  Shifter #(.width(32), .shift("lr")) shifter_1 (.in(B), .\dist (5'b00001), .out(shifter_1_out));
  Shifter #(.width(32)) shifter_2 (.in(B), .\dist (5'b00001), .out(shifter_2_out));
  Multiplexer #(.select(2), .width(32)) multiplexer_1 (
    .in0(B), .in1(shifter_1_out), .in2(shifter_2_out), .out(H), .sel(S));  // open: in3, en
endmodule

module Logic_Circuit (
  input  [31:0] A,
  input  [31:0] B,
  input  [1:0] S,
  output [31:0] G
);

  wire [31:0] and_1_out, not_1_out, or_1_out, xor_1_out;

  assign and_1_out = A & B;  // AND_Gate and_1, 32 bits wide
  assign or_1_out = A | B;  // OR_Gate or_1, 32 bits wide
  assign not_1_out = ~A;  // NOT_Gate not_1, 32 bits wide
  assign xor_1_out = A ^ B;  // XOR_Gate xor_1, 32 bits wide
  Multiplexer #(.select(2), .width(32)) multiplexer_1 (
    .in0(and_1_out), .in1(or_1_out), .in2(xor_1_out), .in3(not_1_out), .out(G), .sel(S));  // open: en
endmodule

module ALU (
  input  [31:0] A,
  input  [31:0] B,
  input  Cin,
  input  [2:0] S,
  output V,
  output Cout,
  output N,
  output [31:0] G,
  output Z
);

  wire and_1_out, and_2_out, nor_1_out, nor_3_out, not_1_out;
  wire [31:0] arithmetic_circuit_1_x, logic_circuit_1_g;

  and and_1 (and_1_out, A[31], B[31]);
  nor nor_1 (nor_1_out, A[31], B[31]);
  Arithmetic_Circuit arithmetic_circuit_1 (
    .A(A), .B(B), .X(arithmetic_circuit_1_x), .Cin(Cin), .S(S[1:0]), .Cout(Cout));
  Logic_Circuit logic_circuit_1 (.A(A), .B(B), .G(logic_circuit_1_g), .S({S[0], Cin}));
  not not_1 (not_1_out, and_1_out);
  Multiplexer #(.width(32)) multiplexer_1 (
    .in0(arithmetic_circuit_1_x), .in1(logic_circuit_1_g), .out(G), .sel(S[2]));  // open: en
  nor nor_2 (Z, G[31], G[30], G[29], G[28], G[27], G[26], G[25], G[24], G[23], G[22], G[21], G[20], G[19], G[18], G[17], G[16], G[15], G[14], G[13], G[12], G[11], G[10], G[9], G[8], G[7], G[6], G[5], G[4], G[3], G[2], G[1], G[0]);
  nor nor_3 (nor_3_out, not_1_out, G[31]);
  and and_2 (and_2_out, G[31], nor_1_out);
  or or_1 (V, nor_3_out, and_2_out);

  assign N = G[31];
endmodule

module Function_unit (
  input  [4:0] SH,
  input  [31:0] A,
  input  [31:0] B,
  input  [3:0] FS,
  output V,
  output C,
  output N,
  output Z,
  output [31:0] F
);

  wire and_1_out;
  wire [31:0] alu_1_g, barrel_shifter_1_h;

  ALU alu_1 (.A(A), .B(B), .Cin(FS[0]), .S(FS[3:1]), .V(V), .Cout(C), .N(N), .G(alu_1_g), .Z(Z));
  and and_1 (and_1_out, FS[2], FS[3]);
  Multiplexer #(.width(32)) multiplexer_1 (
    .in0(alu_1_g), .in1(barrel_shifter_1_h), .out(F), .sel(and_1_out));  // open: en
  Barrel_Shifter barrel_shifter_1 (.B(A), .SH(SH), .H(barrel_shifter_1_h), .S(FS[1:0]));
endmodule

module Instruction_Decoder (
  input  [31:0] Instruction_Code,
  output [3:0] FS,
  output [1:0] MD,
  output RW,
  output CS,
  output [4:0] DA,
  output [4:0] AA,
  output MB,
  output [4:0] BA,
  output PS,
  output [1:0] BS,
  output MW,
  output MA
);

  wire and_1_out, and_2_out, and_3_out, and_4_out, and_5_out, and_6_out, and_7_out, and_8_out, and_9_out,
       and_13_out, and_14_out, and_15_out, and_17_out, and_18_out, and_20_out, and_21_out, and_22_out,
       and_23_out, and_24_out, and_25_out, and_26_out, and_27_out, and_28_out, and_29_out, and_30_out,
       and_31_out, and_33_out, and_34_out, and_35_out, and_36_out, and_37_out, and_38_out, and_39_out,
       and_42_out, not_1_out, not_2_out, not_3_out, not_4_out, not_5_out, not_6_out, not_7_out, not_8_out,
       not_9_out, not_10_out, not_11_out, not_12_out, not_13_out, not_15_out, not_16_out, not_17_out,
       not_18_out, not_19_out, not_20_out, not_21_out, not_22_out, not_23_out, not_24_out, not_25_out,
       not_26_out, not_27_out, not_28_out, not_29_out, not_30_out, not_31_out, not_32_out, not_33_out,
       not_34_out, not_35_out, not_36_out, not_37_out, not_38_out, not_39_out, not_40_out, not_41_out,
       not_42_out, not_43_out, not_44_out, not_45_out, not_46_out, not_47_out, not_48_out, not_49_out,
       not_50_out, not_51_out, not_52_out, not_53_out, not_54_out, not_55_out, not_56_out, not_57_out,
       not_58_out, not_59_out, not_60_out, not_61_out, not_62_out, not_64_out, not_65_out, not_66_out,
       not_67_out, not_68_out, not_69_out, not_70_out, not_71_out, not_72_out, not_73_out, not_74_out,
       not_75_out, not_76_out, not_77_out, not_78_out, not_79_out, not_80_out, not_81_out, not_82_out,
       not_83_out, not_84_out, not_85_out, not_86_out, not_87_out, not_88_out, not_89_out, not_90_out,
       not_91_out, not_92_out, not_93_out, not_94_out, or_1_out, or_2_out, or_3_out, or_4_out, or_5_out,
       or_6_out, or_7_out, or_8_out;

  not not_1 (not_1_out, Instruction_Code[31]);
  not not_2 (not_2_out, Instruction_Code[29]);
  not not_3 (not_3_out, Instruction_Code[27]);
  not not_4 (not_4_out, Instruction_Code[26]);
  not not_5 (not_5_out, Instruction_Code[25]);
  not not_6 (not_6_out, Instruction_Code[26]);
  not not_7 (not_7_out, Instruction_Code[25]);
  not not_8 (not_8_out, Instruction_Code[30]);
  not not_9 (not_9_out, Instruction_Code[29]);
  not not_10 (not_10_out, Instruction_Code[28]);
  not not_11 (not_11_out, Instruction_Code[27]);
  not not_12 (not_12_out, Instruction_Code[25]);
  not not_13 (not_13_out, Instruction_Code[26]);
  not not_14 (CS, or_1_out);
  or or_1 (or_1_out, and_1_out, and_9_out);
  and and_1 (and_1_out, and_2_out, or_2_out);
  and and_2 (and_2_out, not_1_out, Instruction_Code[30], not_2_out, Instruction_Code[28], not_3_out);
  or or_2 (or_2_out, and_3_out, and_4_out, and_5_out);
  and and_3 (and_3_out, not_4_out, not_5_out);
  and and_4 (and_4_out, not_6_out, Instruction_Code[25]);
  and and_5 (and_5_out, Instruction_Code[26], not_7_out);
  and and_6 (and_6_out, Instruction_Code[31], not_8_out, not_9_out, not_10_out);
  and and_7 (and_7_out, not_11_out, Instruction_Code[26], not_12_out);
  and and_8 (and_8_out, Instruction_Code[27], not_13_out, Instruction_Code[25]);
  and and_9 (and_9_out, and_6_out, or_3_out);
  or or_3 (or_3_out, and_7_out, and_8_out);
  not not_15 (not_15_out, Instruction_Code[31]);
  and and_10 (FS[3], not_15_out, Instruction_Code[28]);
  not not_16 (not_16_out, Instruction_Code[31]);
  not not_17 (not_17_out, Instruction_Code[30]);
  not not_18 (not_18_out, Instruction_Code[28]);
  not not_19 (not_19_out, Instruction_Code[27]);
  not not_20 (not_20_out, Instruction_Code[26]);
  not not_21 (not_21_out, Instruction_Code[25]);
  not not_22 (not_22_out, Instruction_Code[29]);
  not not_23 (not_23_out, Instruction_Code[28]);
  not not_24 (not_24_out, Instruction_Code[26]);
  not not_25 (not_25_out, Instruction_Code[29]);
  not not_26 (not_26_out, Instruction_Code[28]);
  not not_27 (not_27_out, Instruction_Code[30]);
  not not_28 (not_28_out, Instruction_Code[29]);
  not not_29 (not_29_out, Instruction_Code[29]);
  not not_30 (not_30_out, Instruction_Code[31]);
  not not_31 (not_31_out, Instruction_Code[28]);
  not not_32 (not_32_out, Instruction_Code[27]);
  not not_33 (not_33_out, Instruction_Code[26]);
  not not_34 (not_34_out, Instruction_Code[25]);
  not not_35 (not_35_out, Instruction_Code[31]);
  not not_36 (not_36_out, Instruction_Code[28]);
  not not_37 (not_37_out, Instruction_Code[27]);
  not not_38 (not_38_out, Instruction_Code[26]);
  not not_39 (not_39_out, Instruction_Code[25]);
  and and_11 (MD[0], not_16_out, not_17_out, Instruction_Code[29], not_18_out, not_19_out, not_20_out, not_21_out);
  and and_12 (MD[1], Instruction_Code[31], Instruction_Code[30], not_22_out, not_23_out, Instruction_Code[27], not_24_out, Instruction_Code[25]);
  and and_13 (and_13_out, Instruction_Code[31], Instruction_Code[30], not_25_out, not_26_out);
  and and_14 (and_14_out, Instruction_Code[31], not_27_out, not_28_out, Instruction_Code[28]);
  or or_4 (or_4_out, and_13_out, and_14_out, and_15_out, and_17_out);
  and and_15 (and_15_out, Instruction_Code[31], Instruction_Code[30], not_29_out, Instruction_Code[28]);
  and and_16 (BS[0], and_18_out, or_4_out);
  and and_17 (and_17_out, not_30_out, Instruction_Code[30], Instruction_Code[29], not_31_out);
  and and_18 (and_18_out, not_32_out, not_33_out, not_34_out);
  and and_19 (MA, not_35_out, Instruction_Code[30], Instruction_Code[29], not_36_out, not_37_out, not_38_out, not_39_out);
  not not_40 (not_40_out, Instruction_Code[31]);
  not not_41 (not_41_out, Instruction_Code[30]);
  not not_42 (not_42_out, Instruction_Code[29]);
  not not_43 (not_43_out, Instruction_Code[28]);
  not not_44 (not_44_out, Instruction_Code[31]);
  not not_45 (not_45_out, Instruction_Code[29]);
  not not_46 (not_46_out, Instruction_Code[28]);
  not not_47 (not_47_out, Instruction_Code[28]);
  not not_48 (not_48_out, Instruction_Code[29]);
  not not_49 (not_49_out, Instruction_Code[28]);
  not not_50 (not_50_out, Instruction_Code[30]);
  not not_51 (not_51_out, Instruction_Code[29]);
  not not_52 (not_52_out, Instruction_Code[29]);
  not not_53 (not_53_out, Instruction_Code[27]);
  not not_54 (not_54_out, Instruction_Code[26]);
  not not_55 (not_55_out, Instruction_Code[25]);
  not not_56 (not_56_out, Instruction_Code[28]);
  not not_57 (not_57_out, Instruction_Code[29]);
  not not_58 (not_58_out, Instruction_Code[31]);
  not not_59 (not_59_out, Instruction_Code[28]);
  not not_60 (not_60_out, Instruction_Code[27]);
  not not_61 (not_61_out, Instruction_Code[26]);
  not not_62 (not_62_out, Instruction_Code[25]);
  and and_20 (and_20_out, not_40_out, not_41_out, not_42_out, not_43_out);
  and and_21 (and_21_out, not_44_out, Instruction_Code[30], not_45_out, not_46_out);
  and and_22 (and_22_out, Instruction_Code[31], Instruction_Code[30], Instruction_Code[29], not_47_out);
  and and_23 (and_23_out, Instruction_Code[31], Instruction_Code[30], not_48_out, not_49_out);
  and and_24 (and_24_out, Instruction_Code[31], not_50_out, not_51_out, Instruction_Code[28]);
  and and_25 (and_25_out, Instruction_Code[31], Instruction_Code[30], not_52_out, Instruction_Code[28]);
  and and_26 (and_26_out, not_53_out, not_54_out, not_55_out);
  and and_27 (and_27_out, Instruction_Code[31], Instruction_Code[30], Instruction_Code[29], not_56_out);
  and and_28 (and_28_out, Instruction_Code[31], Instruction_Code[30], not_57_out, Instruction_Code[28]);
  and and_29 (and_29_out, not_58_out, Instruction_Code[30], Instruction_Code[29], not_59_out);
  and and_30 (and_30_out, not_60_out, not_61_out, not_62_out);
  or or_5 (or_5_out, and_20_out, and_21_out, and_22_out, and_23_out, and_24_out, and_25_out);
  and and_31 (and_31_out, and_26_out, or_5_out);
  not not_63 (RW, and_31_out);
  or or_6 (or_6_out, and_27_out, and_28_out, and_29_out);
  and and_32 (BS[1], and_30_out, or_6_out);
  not not_64 (not_64_out, Instruction_Code[28]);
  not not_65 (not_65_out, Instruction_Code[27]);
  not not_66 (not_66_out, Instruction_Code[25]);
  not not_67 (not_67_out, Instruction_Code[28]);
  not not_68 (not_68_out, Instruction_Code[26]);
  not not_69 (not_69_out, Instruction_Code[27]);
  not not_70 (not_70_out, Instruction_Code[26]);
  not not_71 (not_71_out, Instruction_Code[25]);
  not not_72 (not_72_out, Instruction_Code[31]);
  not not_73 (not_73_out, Instruction_Code[30]);
  not not_74 (not_74_out, Instruction_Code[29]);
  not not_75 (not_75_out, Instruction_Code[31]);
  not not_76 (not_76_out, Instruction_Code[29]);
  not not_77 (not_77_out, Instruction_Code[28]);
  not not_78 (not_78_out, Instruction_Code[27]);
  not not_79 (not_79_out, Instruction_Code[26]);
  not not_80 (not_80_out, Instruction_Code[25]);
  not not_81 (not_81_out, Instruction_Code[29]);
  not not_82 (not_82_out, Instruction_Code[28]);
  not not_83 (not_83_out, Instruction_Code[26]);
  not not_84 (not_84_out, Instruction_Code[30]);
  not not_85 (not_85_out, Instruction_Code[29]);
  not not_86 (not_86_out, Instruction_Code[27]);
  not not_87 (not_87_out, Instruction_Code[26]);
  not not_88 (not_88_out, Instruction_Code[25]);
  not not_89 (not_89_out, Instruction_Code[31]);
  not not_90 (not_90_out, Instruction_Code[29]);
  not not_91 (not_91_out, Instruction_Code[28]);
  not not_92 (not_92_out, Instruction_Code[27]);
  not not_93 (not_93_out, Instruction_Code[26]);
  not not_94 (not_94_out, Instruction_Code[25]);
  and and_33 (and_33_out, not_64_out, not_65_out, Instruction_Code[26], not_66_out);
  and and_34 (and_34_out, not_67_out, Instruction_Code[27], not_68_out, Instruction_Code[25]);
  and and_35 (and_35_out, Instruction_Code[28], not_69_out);
  and and_36 (and_36_out, Instruction_Code[28], Instruction_Code[27], not_70_out, not_71_out);
  and and_37 (and_37_out, not_72_out, not_73_out, not_74_out);
  and and_38 (and_38_out, not_75_out, Instruction_Code[30], not_76_out, not_77_out, not_78_out, not_79_out, not_80_out);
  and and_39 (and_39_out, Instruction_Code[31], Instruction_Code[30], not_81_out, not_82_out, Instruction_Code[27], not_83_out, Instruction_Code[25]);
  and and_40 (PS, Instruction_Code[31], not_84_out, not_85_out, Instruction_Code[28], not_86_out, not_87_out, not_88_out);
  and and_41 (MW, not_89_out, Instruction_Code[30], not_90_out, not_91_out, not_92_out, not_93_out, not_94_out);
  or or_7 (or_7_out, and_33_out, and_34_out, and_35_out, and_36_out);
  and and_42 (and_42_out, and_37_out, or_7_out);
  or or_8 (or_8_out, and_39_out, and_38_out, and_42_out);
  not not_95 (MB, or_8_out);

  assign AA = Instruction_Code[19:15];
  assign BA = Instruction_Code[14:10];
  assign DA = Instruction_Code[24:20];
  assign FS[2:0] = Instruction_Code[27:25];

  // Other names for the same wires on the sheet: OP0 = Instruction_Code[25]; OP1 = Instruction_Code[26];
  //   OP2 = Instruction_Code[27]; _0 = Instruction_Code[0]; _1 = Instruction_Code[1]; _2 = Instruction_Code[2];
  //   _3 = Instruction_Code[3]; _4 = Instruction_Code[4]; _5 = Instruction_Code[5]; _6 = Instruction_Code[6];
  //   _7 = Instruction_Code[7]; _8 = Instruction_Code[8]; _9 = Instruction_Code[9]; SB0 = Instruction_Code[10];
  //   SB1 = Instruction_Code[11]; SB2 = Instruction_Code[12]; SB3 = Instruction_Code[13]; SB4 = Instruction_Code[14];
  //   SA0 = Instruction_Code[15]; SA1 = Instruction_Code[16]; SA2 = Instruction_Code[17]; SA3 = Instruction_Code[18];
  //   SA4 = Instruction_Code[19]; DR0 = Instruction_Code[20]; DR1 = Instruction_Code[21]; DR2 = Instruction_Code[22];
  //   DR3 = Instruction_Code[23]; DR4 = Instruction_Code[24]; OP3 = Instruction_Code[28]; OP4 = Instruction_Code[29];
  //   OP5 = Instruction_Code[30]; OP6 = Instruction_Code[31]
endmodule

module Barrel_Shifter (
  input  [31:0] B,
  input  [4:0] SH,
  input  [1:0] S,
  output [31:0] H
);

  wire [31:0] shifter_1_out, shifter_2_out;

  Shifter #(.width(32), .shift("lr")) shifter_1 (.in(B), .\dist (SH), .out(shifter_1_out));
  Shifter #(.width(32)) shifter_2 (.in(B), .\dist (SH), .out(shifter_2_out));
  Multiplexer #(.select(2), .width(32)) multiplexer_1 (
    .in0(B), .in1(shifter_1_out), .in2(shifter_2_out), .out(H), .sel(S));  // open: in3, en
endmodule

module CPU (
);

  wire and_1_out, and_7_out, and_9_out, and_10_out, C, CLK, comparator_1_eq, comparator_2_eq,
       comparator_3_eq, comparator_4_eq, CS, DHS, H1, H2, HA, HB, instruction_decoder_1_mw,
       instruction_decoder_1_ps, instruction_decoder_1_rw, MA, MB, MW, N, not_2_out, not_3_out, not_5_out,
       not_6_out, or_1_out, or_2_out, or_3_out, or_4_out, PS, RW, RW_q, V, xor_2_out, Z;
  wire [0:0] and_8_out, xor_1_out;
  wire [1:0] and_5_out, BS, instruction_decoder_1_bs, instruction_decoder_1_md, MD, MD_q;
  wire [1:1] not_4_out;
  wire [3:0] FS, instruction_decoder_1_fs;
  wire [4:0] AA, and_2_out, BA, DA, DA_q, instruction_decoder_1_da, SH;
  wire [4:4] not_1_out;
  wire [7:0] PC_q_2;
  wire [23:0] PC_q;
  wire [31:0] adder_1_out, and_6_out, BrA, BUS_B_q, constant_unit_1_output, D_Data, extend_bit_1_output,
       function_unit_1_f, IR_q, multiplexer_1_out, multiplexer_2_out, multiplexer_3_out, PC_1, PC_2_q, RAA,
       ram_1_data, ram_2_data, register_1_q, register_2_q, register_3_q, register_file_1_a_data,
       register_file_1_b_data;

  Register #(.width(32)) PC (.D(multiplexer_1_out), .en(not_1_out[4]), .Q({PC_q_2, PC_q}), .clk(CLK));  // open: clr
  Register #(.width(32)) u_PC_1 (.D(adder_1_out), .en(not_1_out[4]), .Q(PC_1), .clk(CLK));  // open: clr
  not not_1 (not_1_out[4], DHS);
  Register #(.width(32)) PC_2 (.D(PC_1), .en(not_1_out[4]), .Q(PC_2_q), .clk(CLK));  // open: clr
  Adder #(.width(32)) adder_1 (.a({PC_q_2, PC_q}), .b({32{1'b0}}), .out(adder_1_out), .cin(1'b1));  // open: cout
  and and_1 (and_1_out, not_1_out[4], not_4_out[1], instruction_decoder_1_rw);
  Register #(.width(1)) u_RW (.D(and_1_out), .Q(RW_q), .clk(CLK));  // open: en, clr
  Register #(.width(1)) RW_2 (.D(RW_q), .Q(RW), .clk(CLK));  // open: en, clr
  Adder #(.width(32)) adder_2 (.a(PC_2_q), .b(BUS_B_q), .out(BrA));  // open: cin, cout
  Comparator #(.width(5)) comparator_1 (.a(BA), .b(DA), .eq(comparator_1_eq));  // open: gt, lt
  not not_2 (not_2_out, MB);
  Comparator #(.width(5)) comparator_2 (.a(AA), .b(DA), .eq(comparator_2_eq));  // open: gt, lt
  not not_3 (not_3_out, MA);
  not not_4 (not_4_out[1], or_2_out);
  assign and_2_out = {5{not_1_out[4]}} & instruction_decoder_1_da;  // AND_Gate and_2, 5 bits wide
  Register #(.width(5)) u_DA (.D(and_2_out), .Q(DA_q), .clk(CLK));  // open: en, clr
  Register #(.width(5)) DA_2 (.D(DA_q), .Q(DA), .clk(CLK));  // open: en, clr
  and and_3 (H2, comparator_1_eq, not_2_out, or_1_out, RW);
  or or_1 (or_1_out, DA[0], DA[1], DA[2], DA[3], DA[4]);
  and and_4 (H1, comparator_2_eq, not_3_out, or_1_out, RW);
  Multiplexer #(.select(2), .width(32), .enable("false")) multiplexer_1 (
    .in0(adder_1_out), .in1(BrA), .in2(RAA), .in3(BrA), .out(multiplexer_1_out), .sel({BS[1], and_8_out[0]}));
  Extend_Bit extend_bit_1 (.Input(not_4_out[1]), .Output(extend_bit_1_output));
  assign and_5_out = {2{not_1_out[4]}} & {2{not_4_out[1]}} & instruction_decoder_1_bs;  // AND_Gate and_5, 2 bits wide
  Register #(.width(2)) u_MD (.D(instruction_decoder_1_md), .Q(MD_q), .clk(CLK));  // open: en, clr
  Register #(.width(2)) u_BS (.D(and_5_out), .Q(BS), .clk(CLK));  // open: en, clr
  Register #(.width(2)) MD_2 (.D(MD_q), .Q(MD), .clk(CLK));  // open: en, clr
  or or_2 (or_2_out, BS[1], and_8_out[0]);
  assign and_6_out = ram_1_data & extend_bit_1_output;  // AND_Gate and_6, 32 bits wide
  RAM #(.addrWidth(24), .dataWidth(32)) ram_1 (.addr(PC_q), .data(ram_1_data), .clk(CLK));  // open: sel, ld, clr
  and and_7 (and_7_out, not_1_out[4], not_4_out[1], instruction_decoder_1_mw);
  Register #(.width(1)) u_PS (.D(instruction_decoder_1_ps), .Q(PS), .clk(CLK));  // open: en, clr
  Clock clock_1 (.out(CLK));
  Register #(.width(32)) IR (.D(and_6_out), .en(not_1_out[4]), .Q(IR_q), .clk(CLK));  // open: clr
  not not_5 (not_5_out, MA);
  Register #(.width(1)) u_MW (.D(and_7_out), .Q(MW), .clk(CLK));  // open: en, clr
  Register #(.width(4)) u_FS (.D(instruction_decoder_1_fs), .Q(FS), .clk(CLK));  // open: en, clr
  xor xor_1 (xor_1_out[0], V, N);
  and and_8 (and_8_out[0], BS[0], or_3_out);
  or or_3 (or_3_out, BS[1], xor_2_out);
  not not_6 (not_6_out, MB);
  Register #(.width(5)) u_SH (.D(IR_q[4:0]), .Q(SH), .clk(CLK));  // open: en, clr
  xor xor_2 (xor_2_out, PS, Z);
  Constant_Unit constant_unit_1 (.IM(IR_q[14:0]), .Output(constant_unit_1_output), .CS(CS));
  Comparator #(.width(5)) comparator_3 (.a(AA), .b(DA_q), .eq(comparator_3_eq));  // open: gt, lt
  or or_4 (or_4_out, DA_q[0], DA_q[1], DA_q[2], DA_q[3], DA_q[4]);
  Function_unit function_unit_1 (
    .FS(FS), .V(V), .C(C), .N(N), .Z(Z), .A(RAA), .B(BUS_B_q), .F(function_unit_1_f), .SH(SH));
  Register #(.width(32)) register_1 (.D({{31{1'b0}}, xor_1_out[0]}), .Q(register_1_q), .clk(CLK));  // open: en, clr
  Register #(.width(32)) register_2 (.D(function_unit_1_f), .Q(register_2_q), .clk(CLK));  // open: en, clr
  Register_File register_file_1 (
    .D_Data(D_Data), .D_Address(DA), .CLK(CLK), .Write(RW), .A_Address(AA), .B_Address(BA),
    .A_Data(register_file_1_a_data), .B_Data(register_file_1_b_data));
  Instruction_Decoder instruction_decoder_1 (
    .BS(instruction_decoder_1_bs), .FS(instruction_decoder_1_fs), .MD(instruction_decoder_1_md),
    .PS(instruction_decoder_1_ps), .MW(instruction_decoder_1_mw), .MA(MA), .DA(instruction_decoder_1_da),
    .BA(BA), .AA(AA), .Instruction_Code(IR_q), .CS(CS), .RW(instruction_decoder_1_rw), .MB(MB));
  Comparator #(.width(5)) comparator_4 (.a(BA), .b(DA_q), .eq(comparator_4_eq));  // open: gt, lt
  and and_9 (and_9_out, comparator_4_eq, not_6_out, or_4_out, RW_q);
  or or_5 (HB, and_9_out, H2);
  and and_10 (and_10_out, comparator_3_eq, not_5_out, or_4_out, RW_q);
  or or_6 (HA, and_10_out, H1);
  Register #(.width(32)) register_3 (.D(ram_2_data), .Q(register_3_q), .clk(CLK));  // open: en, clr
  Multiplexer #(.width(32), .enable("false")) multiplexer_2 (
    .in0(register_file_1_a_data), .in1(PC_1), .out(multiplexer_2_out), .sel(MA));
  Register #(.width(32)) BUS_A (.D(multiplexer_2_out), .Q(RAA), .clk(CLK));  // open: en, clr
  Multiplexer #(.width(32), .enable("false")) multiplexer_3 (
    .in0(register_file_1_b_data), .in1(constant_unit_1_output), .out(multiplexer_3_out), .sel(MB));
  Register #(.width(32)) BUS_B (.D(multiplexer_3_out), .Q(BUS_B_q), .clk(CLK));  // open: en, clr
  or or_7 (DHS, HB, HA);
  Multiplexer #(.select(2), .width(32), .enable("false")) multiplexer_4 (
    .in0(register_2_q), .in1(register_3_q), .in2(register_1_q), .out(D_Data), .sel(MD));  // open: in3
  RAM #(.addrWidth(24), .dataWidth(32), .bus("separate")) ram_2 (
    .addr(RAA[23:0]), .din(BUS_B_q), .data(ram_2_data), .str(MW), .clk(CLK));  // open: sel, ld, clr
endmodule

module Constant_Unit (
  input  CS,
  input  [14:0] IM,
  output [31:0] Output
);

  wire [16:0] multiplexer_1_out;

  Multiplexer #(.width(17)) multiplexer_1 (
    .in0({17{1'b0}}), .in1({17{1'b1}}), .out(multiplexer_1_out), .sel(IM[14]));  // open: en
  Multiplexer #(.width(17)) multiplexer_2 (
    .in0({17{1'b0}}), .in1(multiplexer_1_out), .out(Output[31:15]), .sel(CS));  // open: en

  assign Output[14:0] = IM;
endmodule

module Extend_Bit (
  input  Input,
  output [31:0] Output
);


  assign Output = {32{Input}};
endmodule
